# Fritzing sketch donkeylight (saved by Fritzing 0.9.3b)

parts:
  LPD8806_RGB_LED_Strip1 = LPD8806 RGB LED Strip
  U1 = NodeMCU V1.0
  S2 = Taiway 100-SP-X-T1 SPDT Miniature Toggle Switch [part_number=100-SP-X-T1-0-0-B1-M1 package=THT]
  U2 = HALL-EFFECT [package=sc70]
  Bauteil1 = Lithium Ion Polymer Battery 3.7v 500mAh [part_number=1578]
  LPD8806_RGB_LED_Strip2 = LPD8806 RGB LED Strip

nets:
  GND: LPD8806_RGB_LED_Strip1.GND#0, U1.GND, U2.GND, Bauteil1.negative, LPD8806_RGB_LED_Strip2.GND#4
  N1: LPD8806_RGB_LED_Strip1.DI, U1.D1
  N2: LPD8806_RGB_LED_Strip1.CI, U1.D2
  VIN: LPD8806_RGB_LED_Strip1.+5V#3, U1.Vin, S2.L1, U2.VCC
  N3: LPD8806_RGB_LED_Strip1.GND#4, LPD8806_RGB_LED_Strip2.GND#0
  N4: LPD8806_RGB_LED_Strip1.DO, LPD8806_RGB_LED_Strip2.DI
  N5: LPD8806_RGB_LED_Strip1.CO, LPD8806_RGB_LED_Strip2.CI
  N6: LPD8806_RGB_LED_Strip1.+5V#7, LPD8806_RGB_LED_Strip2.+5V
  N7: U1.D3, U2.OUT
  N8: S2.COM, Bauteil1.positive

notes:
  5 PIN connector
  APA102
  (Adafruit Dotstar)
  LiIon battery 3.7V or
  USB powerbank 5V
  hall-effect sensor
  simple on/off switch
  magnet

custom parts:
  LPD8806 RGB LED Strip: Digitally addressable RGB LED strip
  NodeMCU V1.0: ESP8266 based NodeMCU
  Lithium Ion Polymer Battery 3.7v 500mAh: Lithium ion polymer (also known as 'lipo' or 'lipoly') batteries are thin, light and powerful. The output ranges from 4.2V when completely charged to 3.7V. This battery has a capacity of 500mAh for a total of about 1.9 Wh. The batteries come pre-attached with a genuine 2-pin JST-PH connector as shown and include the necessary protection circuitry.
